// Logisim project CPU2.circ as structural Verilog
module mboard (
);

  wire and_1_out, and_2_out, and_3_out, and_4_out, clock_1_out, cpu_1_we, not_1_out;
  wire [7:0] cpu_1_dout, ram_1_data, rom_1_data;
  wire [15:0] cpu_1_addr;

  cpu cpu_1 (.CLK(clock_1_out), .DIN(cpu_1_dout), .ADDR(cpu_1_addr), .DOUT(cpu_1_dout), .WE(cpu_1_we));
  Clock clock_1 (.out(clock_1_out));
  // Probe on cpu_1_dout
  // Probe on cpu_1_addr
  and and_1 (and_1_out, ~cpu_1_addr[14], ~cpu_1_addr[15]);  // AND_Gate
  not not_1 (not_1_out, cpu_1_we);
  and and_2 (and_2_out, cpu_1_addr[14], cpu_1_addr[15]);
  and and_3 (and_3_out, not_1_out, and_1_out);
  and and_4 (and_4_out, and_1_out, ~not_1_out);  // AND_Gate
  Multiplexer #(.disabled("Z"), .width(8)) multiplexer_1 (
    .in1(ram_1_data), .out(cpu_1_dout), .sel(and_3_out));  // open: in0
  Multiplexer #(.disabled("Z"), .width(8)) multiplexer_2 (
    .in1(rom_1_data), .out(cpu_1_dout), .sel(and_2_out));  // open: in0
  RAM #(.addrWidth(14), .databus("bidir"), .enables("line")) ram_1 (
    .addr(cpu_1_addr[13:0]), .data(ram_1_data));  // open: we, oe, clk
  Multiplexer #(.disabled("Z"), .width(8)) multiplexer_3 (
    .in1(cpu_1_dout), .out(ram_1_data), .sel(and_4_out));  // open: in0
  ROM #(.addrWidth(14)) rom_1 (.addr(cpu_1_addr[13:0]), .data(rom_1_data));
endmodule

module cpu (
  input  [7:0] DIN,
  input  CLK,
  output [7:0] DOUT,
  output [15:0] ADDR,
  output WE
);

  wire AB_sh, AB_sl, CD_sh, CD_sl, counter_1_carry, HL_sh, HL_sl, PC_ct, PC_idh, PC_idl, PC_ldh, PC_ldl,
       SP_sh, SP_sl;
  wire [3:0] alu_1_z, ctrl_1_ab, ctrl_1_cd, ctrl_1_hl, ctrl_1_pc, ctrl_1_sp;
  wire [5:0] ctrl_1_alu;
  wire [7:0] AB_tohigh, AB_tolow, CD_tohigh, CD_tolow, counter_1_q, counter_2_q, ctrl_1_irprobe, HL_tohigh,
       HL_tolow, multiplexer_2_out, register_1_q, register_2_q, register_3_q, register_4_q, register_5_q,
       register_6_q, register_7_q, register_8_q, SP_tohigh, SP_tolow, undriven;

  // Probe on ctrl_1_irprobe
  // Probe on multiplexer_2_out
  Multiplexer #(.disabled("Z"), .width(8)) multiplexer_1 (.in1(multiplexer_2_out), .out(DOUT), .sel(WE));  // open: in0
  Multiplexer #(.disabled("Z"), .width(8)) multiplexer_2 (.in0(DIN), .out(multiplexer_2_out), .sel(WE));  // open: in1
  ctrl ctrl_1 (
    .Clk(CLK), .DATABUS(multiplexer_2_out), .FLAG(alu_1_z), .PC(ctrl_1_pc), .ALU(ctrl_1_alu),
    .IRPROBE(ctrl_1_irprobe), .CD(ctrl_1_cd), .AB(ctrl_1_ab), .HL(ctrl_1_hl), .SP(ctrl_1_sp), .M(WE));
  Counter counter_1 (
    .load(PC_ldl), .D(undriven), .count(PC_ct), .Q(counter_1_q), .carry(counter_1_carry), .up(PC_idl),
    .clk(CLK));  // open: clr
  Register register_1 (.D(AB_tolow), .en(AB_sl), .Q(register_1_q), .clk(CLK));  // open: clr
  pcctrl PC (
    .op1(ctrl_1_pc[1]), .op0(ctrl_1_pc[0]),
    .in8({multiplexer_2_out[7], undriven[7], multiplexer_2_out[6], undriven[6], multiplexer_2_out[5], undriven[5], multiplexer_2_out[4], undriven[4], multiplexer_2_out[3], undriven[3], multiplexer_2_out[2], undriven[2], multiplexer_2_out[1], undriven[1], multiplexer_2_out[0], undriven[0]}),
    .olow(counter_1_q), .ohi(counter_2_q), .op3(ctrl_1_pc[3]), .op2(ctrl_1_pc[2]), .ct(PC_ct), .idh(PC_idh),
    .idl(PC_idl), .ldh(PC_ldh), .ldl(PC_ldl), .out16(ADDR), .out8(multiplexer_2_out));
  Counter counter_2 (
    .load(PC_ldh), .D(counter_1_q), .count(counter_1_carry), .Q(counter_2_q), .up(PC_idh), .clk(CLK));  // open: carry, clr
  regctrl AB (
    .OP3(ctrl_1_ab[3]), .OP2(ctrl_1_ab[2]), .OP1(ctrl_1_ab[1]), .OP0(ctrl_1_ab[0]), .In8(multiplexer_2_out),
    .FromLow(register_1_q), .FromHigh(register_2_q), .In16(ADDR), .Out8(multiplexer_2_out), .SL(AB_sl),
    .ToLow(AB_tolow), .SH(AB_sh), .ToHigh(AB_tohigh), .Out16(ADDR));
  Register register_2 (.D(AB_tohigh), .en(AB_sh), .Q(register_2_q), .clk(CLK));  // open: clr
  ALU alu_1 (
    .A(register_1_q), .B(register_2_q), .cin(ctrl_1_alu[5]), .op3(ctrl_1_alu[4]), .op2(ctrl_1_alu[3]),
    .op1(ctrl_1_alu[2]), .op0(ctrl_1_alu[1]), .X(ctrl_1_alu[0]), .O(multiplexer_2_out), .Z(alu_1_z[0]),
    .G(alu_1_z[1]), .E(alu_1_z[2]), .C(alu_1_z[3]));
  regctrl SP (
    .OP3(ctrl_1_sp[3]), .OP2(ctrl_1_sp[2]), .OP1(ctrl_1_sp[1]), .OP0(ctrl_1_sp[0]), .In8(multiplexer_2_out),
    .FromLow(register_3_q), .FromHigh(register_5_q), .In16(ADDR), .Out8(multiplexer_2_out), .SL(SP_sl),
    .ToLow(SP_tolow), .SH(SP_sh), .ToHigh(SP_tohigh), .Out16(ADDR));
  Register register_3 (.D(SP_tolow), .en(SP_sl), .Q(register_3_q), .clk(CLK));  // open: clr
  Register register_4 (.D(CD_tolow), .en(CD_sl), .Q(register_4_q), .clk(CLK));  // open: clr
  Register register_5 (.D(SP_tohigh), .en(SP_sh), .Q(register_5_q), .clr(CLK));  // open: clk
  regctrl CD (
    .OP3(ctrl_1_cd[3]), .OP2(ctrl_1_cd[2]), .OP1(ctrl_1_cd[1]), .OP0(ctrl_1_cd[0]), .In8(multiplexer_2_out),
    .FromLow(register_4_q), .FromHigh(register_6_q), .In16(ADDR), .Out8(multiplexer_2_out), .SL(CD_sl),
    .ToLow(CD_tolow), .SH(CD_sh), .ToHigh(CD_tohigh), .Out16(ADDR));
  Register register_6 (.D(CD_tohigh), .en(CD_sh), .Q(register_6_q), .clk(CLK));  // open: clr
  Register register_7 (.D(HL_tolow), .en(HL_sl), .Q(register_7_q), .clk(CLK));  // open: clr
  // Probe on ADDR
  regctrl HL (
    .OP3(ctrl_1_hl[3]), .OP2(ctrl_1_hl[2]), .OP1(ctrl_1_hl[1]), .OP0(ctrl_1_hl[0]), .In8(multiplexer_2_out),
    .FromLow(register_7_q), .FromHigh(register_8_q), .In16(ADDR), .Out8(multiplexer_2_out), .SL(HL_sl),
    .ToLow(HL_tolow), .SH(HL_sh), .ToHigh(HL_tohigh), .Out16(ADDR));
  Register register_8 (.D(HL_tohigh), .en(HL_sh), .Q(register_8_q), .clk(CLK));  // open: clr
endmodule

module ALU (
  input  [7:0] A,
  input  [7:0] B,
  input  cin,
  input  op3,
  input  op2,
  input  op1,
  input  op0,
  input  X,
  output [7:0] O,
  output Z,
  output G,
  output E,
  output C
);

  wire adder_1_cout, subtractor_1_bout;
  wire [7:0] adder_1_out, and_1_out, demultiplexer_1_out0, demultiplexer_1_out1, demultiplexer_1_out2,
       demultiplexer_1_out3, demultiplexer_1_out4, demultiplexer_1_out5, demultiplexer_1_out6,
       demultiplexer_1_out7, demultiplexer_2_out0, demultiplexer_2_out1, demultiplexer_2_out2,
       demultiplexer_2_out3, demultiplexer_2_out4, demultiplexer_2_out6, demultiplexer_2_out7, not_1_out,
       or_1_out, shifter_1_out, shifter_2_out, subtractor_1_out, xor_1_out;

  Demultiplexer #(.select(3), .width(8)) demultiplexer_1 (
    .out0(demultiplexer_1_out0), .out1(demultiplexer_1_out1), .out2(demultiplexer_1_out2),
    .out3(demultiplexer_1_out3), .out4(demultiplexer_1_out4), .out5(demultiplexer_1_out5),
    .out6(demultiplexer_1_out6), .out7(demultiplexer_1_out7), .in(A), .sel({op2, op1, op0}));
  Demultiplexer #(.select(3), .width(8)) demultiplexer_2 (
    .out0(demultiplexer_2_out0), .out1(demultiplexer_2_out1), .out2(demultiplexer_2_out2),
    .out3(demultiplexer_2_out3), .out4(demultiplexer_2_out4), .out6(demultiplexer_2_out6),
    .out7(demultiplexer_2_out7), .in(B), .sel({op2, op1, op0}));  // open: out5
  Adder adder_1 (.a(demultiplexer_1_out0), .b(demultiplexer_2_out0), .out(adder_1_out), .cin(cin), .cout(adder_1_cout));
  Subtractor subtractor_1 (
    .a(demultiplexer_1_out1), .b(demultiplexer_2_out1), .out(subtractor_1_out), .bin(cin),
    .bout(subtractor_1_bout));
  assign and_1_out = demultiplexer_1_out2 & demultiplexer_2_out2;  // AND_Gate and_1, 8 bits wide
  assign or_1_out = demultiplexer_1_out3 | demultiplexer_2_out3;  // OR_Gate or_1, 8 bits wide
  assign xor_1_out = demultiplexer_1_out4 ^ demultiplexer_2_out4;  // XOR_Gate xor_1, 8 bits wide
  assign not_1_out = ~demultiplexer_1_out5;  // NOT_Gate not_1, 8 bits wide
  Shifter #(.shift("rl")) shifter_1 (
    .in(demultiplexer_1_out6), .\dist (demultiplexer_2_out6[2:0]), .out(shifter_1_out));
  Shifter #(.shift("rr")) shifter_2 (
    .in(demultiplexer_1_out7), .\dist (demultiplexer_2_out7[2:0]), .out(shifter_2_out));
  Multiplexer #(.disabled("Z"), .enable("true"), .select(3), .width(8)) multiplexer_1 (
    .in0(adder_1_out), .in1(subtractor_1_out), .in2(and_1_out), .in3(or_1_out), .in4(xor_1_out),
    .in5(not_1_out), .in6(shifter_1_out), .in7(shifter_2_out), .out(O), .sel({op2, op1, op0}), .en(X));
  nor nor_1 (Z, A[0], A[1], A[2], A[3], A[4], A[5], A[6], A[7]);
  Comparator comparator_1 (.a(A), .b(B), .gt(G), .eq(E));  // open: lt
  or or_2 (C, adder_1_cout, subtractor_1_bout);

  // Notes on the sheet:
  //   A: pull=down
  //   B: pull=down
endmodule

module ctrl (
  input  Clk,
  input  [7:0] DATABUS,
  input  [3:0] FLAG,
  output [7:0] IRPROBE,
  output [3:0] CD,
  output [3:0] AB,
  output [3:0] HL,
  output [3:0] SP,
  output M,
  output [3:0] PC,
  output [5:0] ALU
);

  wire pull_resistor_1_node;
  wire [2:0] counter_1_q, rom_1_data;
  wire [3:0] and_1_out, decoder_1_out3, register_2_q;
  wire [11:11] or_1_out;
  wire [31:30] rom_1_data_2;

  Register register_1 (.D(DATABUS), .en(rom_1_data[1]), .Q(IRPROBE), .clk(Clk));  // open: clr
  Pull_Resistor #(.pull(1)) pull_resistor_1 (.node(pull_resistor_1_node));
  Decoder #(.enable("false"), .select(2)) decoder_1 (
    .out0(decoder_1_out3[3]), .out1(decoder_1_out3[2]), .out2(decoder_1_out3[1]), .out3(decoder_1_out3[0]),
    .sel(IRPROBE[1:0]));
  Register #(.width(4)) register_2 (.D(FLAG), .en(rom_1_data[2]), .Q(register_2_q), .clk(Clk));  // open: clr
  Counter #(.max('h7), .trigger("falling"), .width(3)) counter_1 (
    .count(pull_resistor_1_node), .Q(counter_1_q), .up(pull_resistor_1_node), .clk(Clk), .clr(rom_1_data[0]));  // open: load, D, carry
  assign and_1_out = decoder_1_out3 & register_2_q;  // AND_Gate and_1, 4 bits wide
  or or_1 (or_1_out[11], and_1_out[0], and_1_out[1], and_1_out[2], and_1_out[3]);
  ROM #(.addrWidth(12), .dataWidth(32)) rom_1 (
    .addr({or_1_out[11], IRPROBE, counter_1_q}), .data({rom_1_data_2, rom_1_data, CD, AB, HL, SP, M, PC, ALU}));
  Pull_Resistor pull_resistor_2 (.node({rom_1_data_2, rom_1_data, CD, AB, HL, SP, M, PC, ALU}));

  // Notes on the sheet:
  //   Clk: pull=down
  //   contents of rom_1 (hex, n*v repeats v):
  //   10000280 8000000 6*0 10000280 7*0 10000280 7*0 10000280 7*0 10000280 7*0 10000280 7*0 10000280 7*0
  //   10000280 7*0 10000280 8000000 6*0 10000280 7*0 10000280 7*0 10000280 7*0 10000280 7*0 10000280 7*0
  //   10000280 7*0 10000280 7*0 10000280 400280 8000000 5*0 10000280 7*0 10000280 7*0 10000280 7*0
  //   10000280 7*0 10000280 7*0 10000280 7*0 10000280 7*0 10000280 7*0 10000280 7*0 10000280 7*0 10000280
  //   7*0 10000280 7*0 10000280 7*0 10000280 7*0 10000280 7*0 10000280 7*0 10000280 7*0 10000280 7*0
  //   10000280 7*0 10000280 7*0 10000280 7*0 10000280 7*0 10000280 7*0 10000280 7*0 10000280 7*0 10000280
  //   7*0 10000280 7*0 10000280 7*0 10000280 7*0 10000280 7*0 10000280 7*0 10000280 7*0 10000280 7*0
  //   10000280 7*0 10000280 7*0 10000280 7*0 10000280 7*0 10000280 7*0 10000280 7*0 10000280 7*0 10000280
  //   7*0 10000280 7*0 10000280 7*0 10000280 7*0 10000280 7*0 10000280 7*0 10000280 7*0 10000280 7*0
  //   10000280 7*0 10000280 7*0 10000280 7*0 10000280 7*0 10000280 7*0 10000280 7*0 10000280 7*0 10000280
  //   7*0 10000280 7*0 10000280 7*0 10000280 7*0 10000280 7*0 10000280 7*0 10000280 7*0 10000280 7*0
  //   10000280 7*0 10000280 7*0 10000280 7*0 10000280 7*0 10000280 7*0 10000280 7*0 10000280 7*0 10000280
  //   7*0 10000280 7*0 10000280 7*0 10000280 7*0 10000280 7*0 10000280 7*0 10000280 7*0 10000280 7*0
  //   10000280 7*0 10000280 7*0 10000280 7*0 10000280 7*0 10000280 7*0 10000280 7*0 10000280 7*0 10000280
  //   7*0 10000280 7*0 10000280 7*0 10000280 7*0 10000280 7*0 10000280 7*0 10000280 7*0 10000280 7*0
  //   10000280 7*0 10000280 7*0 10000280 7*0 10000280 7*0 10000280 7*0 10000280 7*0 10000280 7*0 10000280
  //   7*0 10000280 7*0 10000280 7*0 10000280 7*0 10000280 7*0 10000280 7*0 10000280 7*0 10000280 7*0
  //   10000280 7*0 10000280 7*0 10000280 7*0 10000280 7*0 10000280 7*0 10000280 7*0 10000280 7*0 10000280
  //   7*0 10000280 7*0 10000280 7*0 10000280 7*0 10000280 7*0 10000280 7*0 10000280 7*0 10000280 7*0
  //   10000280 7*0 10000280 7*0 10000280 7*0 10000280 7*0 10000280 7*0 10000280 7*0 10000280 7*0 10000280
  //   7*0 10000280 7*0 10000280 7*0 10000280 7*0 10000280 7*0 10000280 7*0 10000280 7*0 10000280 7*0
  //   10000280 7*0 10000280 7*0 10000280 7*0 10000280 7*0 10000280 7*0 10000280 7*0 10000280 7*0 10000280
  //   7*0 10000280 7*0 10000280 7*0 10000280 7*0 10000280 7*0 10000280 7*0 10000280 7*0 10000280 7*0
  //   10000280 7*0 10000280 7*0 10000280 7*0 10000280 7*0 10000280 7*0 10000280 7*0 10000280 7*0 10000280
  //   7*0 10000280 7*0 10000280 7*0 10000280 7*0 10000280 7*0 10000280 7*0 10000280 7*0 10000280 7*0
  //   10000280 7*0 10000280 7*0 10000280 7*0 10000280 7*0 10000280 7*0 10000280 7*0 10000280 7*0 10000280
  //   7*0 10000280 7*0 10000280 7*0 10000280 7*0 10000280 7*0 10000280 7*0 10000280 7*0 10000280 7*0
  //   10000280 7*0 10000280 7*0 10000280 7*0 10000280 7*0 10000280 7*0 10000280 7*0 10000280 7*0 10000280
  //   7*0 10000280 7*0 10000280 7*0 10000280 7*0 10000280 7*0 10000280 7*0 10000280 7*0 10000280 7*0
  //   10000280 7*0 10000280 7*0 10000280 7*0 10000280 7*0 10000280 7*0 10000280 7*0 10000280 7*0 10000280
  //   7*0 10000280 7*0 10000280 7*0 10000280 7*0 10000280 7*0 10000280 7*0 10000280 7*0 10000280 7*0
  //   10000280 7*0 10000280 7*0 10000280 7*0 10000280 7*0 10000280 7*0 10000280 7*0 10000280 7*0 10000280
  //   7*0 10000280 7*0 10000280 7*0 10000280 7*0 10000280 7*0 10000280 7*0 10000280 7*0 10000280 7*0
  //   10000280 7*0 10000280 7*0 10000280 7*0 10000280 7*0 10000280 7*0 10000280 7*0 10000280 7*0 10000280
  //   7*0 10000280 7*0 10000280 7*0 10000280
endmodule

module PC (
  input  PC_OP1,
  input  CLK,
  input  [7:0] DATAIN,
  input  E8,
  input  E16,
  input  PC_OP0,
  output [15:0] PROBE,
  output [15:0] ADDROUT,
  output [7:0] DATAOUT
);

  wire and_1_out, and_2_out, counter_1_carry;

  and and_1 (and_1_out, PC_OP1, ~PC_OP0);  // AND_Gate
  and and_2 (and_2_out, ~PC_OP1, PC_OP0);  // AND_Gate
  Counter counter_1 (
    .load(and_2_out), .D(DATAIN), .count(PC_OP1), .Q(PROBE[7:0]), .carry(counter_1_carry), .up(and_1_out),
    .clk(CLK));  // open: clr
  Counter counter_2 (
    .load(and_2_out), .D(PROBE[7:0]), .count(counter_1_carry), .Q(PROBE[15:8]), .up(and_1_out), .clk(CLK));  // open: carry, clr
  assign ADDROUT = E16 ? PROBE : 16'bz;  // Controlled_Buffer controlled_buffer_1
  assign DATAOUT = E8 ? PROBE[15:8] : 8'bz;  // Controlled_Buffer controlled_buffer_2

  // Notes on the sheet:
  //   PROBE: pull=down
endmodule

module regctrl (
  input  [15:0] In16,
  input  [7:0] In8,
  input  OP3,
  input  OP2,
  input  OP1,
  input  OP0,
  input  [7:0] FromLow,
  input  [7:0] FromHigh,
  output [7:0] Out8,
  output [15:0] Out16,
  output SL,
  output [7:0] ToLow,
  output SH,
  output [7:0] ToHigh
);

  wire and_3_out, and_4_out, and_5_out;

  and and_1 (SH, OP3, OP2);
  and and_2 (SL, OP3, ~OP2);  // AND_Gate
  and and_3 (and_3_out, ~OP3, OP2);  // AND_Gate
  and and_4 (and_4_out, OP1, OP0);
  and and_5 (and_5_out, ~OP1, OP0);  // AND_Gate
  Multiplexer #(.disabled("Z"), .enable("true"), .width(8)) multiplexer_1 (
    .in0(FromLow), .in1(FromHigh), .out(Out8), .sel(and_4_out), .en(OP1));
  Multiplexer #(.disabled("Z"), .width(8)) multiplexer_2 (.in0(In8), .in1(In16[7:0]), .out(ToLow), .sel(and_3_out));
  Multiplexer #(.disabled("Z"), .width(8)) multiplexer_3 (.in0(In8), .in1(In16[15:8]), .out(ToHigh), .sel(and_3_out));
  assign Out16 = and_5_out ? {FromHigh, FromLow} : 16'bz;  // Controlled_Buffer controlled_buffer_1
endmodule

module pcctrl (
  input  [7:0] olow,
  input  [7:0] in8,
  input  op3,
  input  [7:0] ohi,
  input  op2,
  input  op1,
  input  op0,
  output [15:0] out16,
  output [7:0] pcin,
  output [7:0] out8,
  output idh,
  output idl,
  output ldh,
  output ldl,
  output ct
);

  and and_1 (idh, op1, ~op0);  // AND_Gate
  and and_2 (ldh, ~op1, op0);  // AND_Gate
  assign out16 = op3 ? {ohi, olow} : 16'bz;  // Controlled_Buffer controlled_buffer_1
  assign out8 = op2 ? ohi : 8'bz;  // Controlled_Buffer controlled_buffer_2

  assign ct = op1;
  assign idl = idh;
  assign ldl = ldh;
  assign pcin = in8;
endmodule

module REGFILE (
  input  [7:0] in_1,
  input  [15:0] in_2,
  input  in_3,
  input  [1:0] in_4,
  input  in_5,
  input  [1:0] in_6,
  input  in_7,
  input  in_8,
  input  in_9,
  input  [2:0] in_10,
  input  in_11,
  input  [1:0] in_12,
  input  in_13,
  input  in_14,
  input  in_15,
  input  in_16,
  input  in_17,
  input  in_18,
  input  in_19,
  input  in_20,
  input  in_21,
  output [7:0] out_22,
  output [15:0] out_23
);

  wire decoder_1_out0, decoder_1_out1, decoder_1_out2, decoder_1_out3, decoder_2_out0, decoder_2_out1,
       decoder_2_out2, decoder_2_out3, or_1_out, or_2_out, or_3_out, or_4_out, or_5_out, PCL_carry, SPL_carry;
  wire [7:0] A_q, B_q, C_q, D_q, H_q, L_q, multiplexer_1_out, multiplexer_2_out, PCH_q, PCL_q, SPH_q, SPL_q;

  Decoder #(.select(2)) decoder_1 (
    .out0(decoder_1_out0), .out1(decoder_1_out1), .out2(decoder_1_out2), .out3(decoder_1_out3), .sel(in_4),
    .en(in_5));
  Decoder #(.select(2)) decoder_2 (
    .out0(decoder_2_out0), .out1(decoder_2_out1), .out2(decoder_2_out2), .out3(decoder_2_out3), .sel(in_6),
    .en(in_7));
  or or_1 (or_1_out, in_3, in_9);
  or or_2 (or_2_out, decoder_1_out0, in_3, decoder_2_out0);
  or or_3 (or_3_out, decoder_1_out1, in_3, decoder_2_out1);
  or or_4 (or_4_out, decoder_1_out2, in_9, decoder_2_out2);
  or or_5 (or_5_out, decoder_1_out3, in_9, decoder_2_out3);
  Multiplexer #(.width(8)) multiplexer_1 (.in0(in_1), .in1(in_2[7:0]), .out(multiplexer_1_out), .sel(or_1_out));
  Register A (.D(multiplexer_1_out), .en(or_2_out), .Q(A_q), .clk(in_21));  // open: clr
  Register C (.D(multiplexer_1_out), .en(or_4_out), .Q(C_q), .clk(in_21));  // open: clr
  Register L (.D(multiplexer_1_out), .en(in_13), .Q(L_q), .clk(in_21));  // open: clr
  Counter PCL (
    .load(in_16), .D(multiplexer_1_out), .count(in_17), .Q(PCL_q), .carry(PCL_carry), .up(in_15), .clk(in_21));  // open: clr
  Counter SPL (
    .load(in_19), .D(multiplexer_1_out), .count(in_20), .Q(SPL_q), .carry(SPL_carry), .up(in_18), .clk(in_21));  // open: clr
  Multiplexer #(.width(8)) multiplexer_2 (.in0(in_1), .in1(in_2[15:8]), .out(multiplexer_2_out), .sel(or_1_out));
  Register B (.D(multiplexer_2_out), .en(or_3_out), .Q(B_q), .clk(in_21));  // open: clr
  Register D (.D(multiplexer_2_out), .en(or_5_out), .Q(D_q), .clk(in_21));  // open: clr
  Register H (.D(multiplexer_2_out), .en(in_14), .Q(H_q), .clk(in_21));  // open: clr
  Counter PCH (.load(in_16), .D(PCL_q), .count(PCL_carry), .Q(PCH_q), .up(in_15), .clk(in_21));  // open: carry, clr
  Counter SPH (.load(in_19), .D(SPL_q), .count(SPL_carry), .Q(SPH_q), .up(in_18), .clk(in_21));  // open: carry, clr
  Multiplexer #(.disabled("Z"), .enable("true"), .select(3), .width(8)) multiplexer_3 (
    .in0(A_q), .in1(B_q), .in2(C_q), .in3(D_q), .in4(PCL_q), .in5(PCH_q), .in6(SPL_q), .in7(SPH_q),
    .out(out_22), .sel(in_10), .en(in_8));
  Multiplexer #(.disabled("Z"), .enable("true"), .select(2), .width(16)) multiplexer_4 (
    .in0({B_q, A_q}), .in1({D_q, C_q}), .in2({PCH_q, PCL_q}), .in3({SPH_q, SPL_q}), .out(out_23),
    .sel(in_12), .en(in_11));
endmodule
